# Fritzing sketch Motor test bench (saved by Fritzing 0.9.3b)

parts:
  Componente1 = Arduino Uno (Rev3) - ICSP
  S1 = L298N module
  Componente2 = AC712 module
  Componente3 = HX711 Module
  Load_Cell1 = Load Cell
  M1 = DC Motor
  Q1 = PHOTOTRANSISTOR REFLECTIVE OBJECT SENSOR [package=qrb1114-side]
  R1 = Resistor [tolerance=±5% resistance=1k package="0603 [SMD]"]

nets:
  N1: Componente1.A0, S1.M1-01, Componente2.2, Componente2.OUT
  N2: Componente1.D10_PWM/SS, Componente3.DO/RX
  N3: Componente1.D11_PWM/MOSI, Componente3.CK/TX
  GND: Componente1.GND, S1.GND, Componente2.GND, Componente3.GND, Q1.C, Q1.K
  N4: Componente1.D3_PWM, Q1.A
  N5: Componente1.D5_PWM, S1.ENA
  N6: Componente1.D6_PWM, S1.IN1
  N7: Componente1.D7, S1.IN2
  N8: Componente1.IOREF, Componente3.VCC
  5V: Componente1.5V, Componente2.VCC
  N9: Componente1.VIN, R1.Pin_1
  N10: S1.M1-02, M1.pin_1
  N11: Componente2.1, M1.pin_2
  N12: Componente3.E+, Load_Cell1.wire1
  N13: Componente3.E-, Load_Cell1.wire2
  N14: Componente3.A+, Load_Cell1.wire3
  N15: Componente3.A-, Load_Cell1.wire4
  N16: Q1.E, R1.Pin_0

notes:
  12V

custom parts:
  L298N module: h-bridge
  HX711 Module: HX711 is a precision 24-bit analog-to-digital converter (ADC) designed for weigh scales and industrial control applications to interface directly with a bridge sensor.
  Load Cell: A rectangle load cell/weighting pressure Sensor with four wires - Red, white, black, green. Normally corresponding with E+, E-, A+, A- respectively.
